# Fritzing sketch circuit_diagram (saved by Fritzing 1.0.8)

parts:
  R1 = Resistor [tolerance=±5% power=0.25W resistance=220 package=THT]
  HC-SR04_Sensor_1 = HC-SR04 Ultrasonic Distance Sensor
  A1 = Esp32-c3 super mini
  Part1 = 12 NeoPixel Ring [part_number=1643]
  Part3 = Lilypad Power Supply
  R2 = Resistor [tolerance=±5% power=0.25W resistance=220 package=THT]
  R3 = Resistor [tolerance=±5% power=0.25W resistance=220 package=THT]
  R4 = Resistor [tolerance=±5% power=0.25W resistance=220 package=THT]
  R5 = Resistor [tolerance=±5% power=0.25W resistance=220 package=THT]
  R6 = Resistor [tolerance=±5% power=0.25W resistance=220 package=THT]
  Part4 = LilyPad Slide Switch

nets:
  N1: R1.Pin_0, R2.Pin_1
  N2: R1.Pin_1, A1.Pin_10, R3.Pin_0
  VCC: HC-SR04_Sensor_1.VCC, A1.Pin_16, Part1.VDD, R3.Pin_1, Part4.OFF
  N3: HC-SR04_Sensor_1.TRIG, A1.Pin_1
  N4: HC-SR04_Sensor_1.ECHO, R5.Pin_1
  GND: HC-SR04_Sensor_1.GND, A1.Pin_15, Part1.GND, Part3.GND, R2.Pin_0, R6.Pin_0
  N5: A1.Pin_2, R4.Pin_1, R5.Pin_0
  N6: A1.Pin_11, Part1.IN
  N7: Part3.+, Part4.ON
  N8: R4.Pin_0, R6.Pin_1

custom parts:
  Esp32-c3 super mini: ESP32-C3 Development Board ESP32 SuperMini Development Board ESP32 Development Board WiFi Bluetooth.
